// Digital circuit lutcomp.dig as structural Verilog
module lutcomp (
  input  RESET,
  input  clk
);

  wire CLK_t, CLK_t_t, HALT, not_2_out, switch_1_b, uc_1_a0_cp, uc_1_a1_cp, uc_1_a2_cp, uc_1_addr_oe,
       uc_1_alu_cp, uc_1_alu_oe, uc_1_in1_cp, uc_1_mem_cp, uc_1_mem_oe, uc_1_pc_inc, uc_1_pc_spe,
       uc_1_ttyout_cp, uc_1_w_cp, uc_1_w_oe, uc_1_x_cp, uc_1_x_oe, uc_1_y_cp, uc_1_y_oe, uc_1_z_cp, uc_1_z_oe;
  wire [2:0] uc_1_alu_op;
  wire [7:0] uc_1_data;
  wire [23:0] pc_1_pc;

  and and_1 (CLK_t, clk, HALT);
  not not_1 (CLK_t_t, CLK_t);
  uc uc_1 (
    .CLK(CLK_t_t), .RESET(RESET), .DATA(uc_1_data), .ADDR_OE(uc_1_addr_oe), .ALU_OP(uc_1_alu_op),
    .PC_INC(uc_1_pc_inc), .IN1_CP(uc_1_in1_cp), .ALU_CP(uc_1_alu_cp), .MEM_CP(uc_1_mem_cp), .W_CP(uc_1_w_cp),
    .X_CP(uc_1_x_cp), .Y_CP(uc_1_y_cp), .Z_CP(uc_1_z_cp), .A0_CP(uc_1_a0_cp), .A1_CP(uc_1_a1_cp),
    .A2_CP(uc_1_a2_cp), .TTYOUT_CP(uc_1_ttyout_cp), .HALT(HALT), .ALU_OE(uc_1_alu_oe), .MEM_OE(uc_1_mem_oe),
    .PC_SPE(uc_1_pc_spe), .W_OE(uc_1_w_oe), .X_OE(uc_1_x_oe), .Y_OE(uc_1_y_oe), .Z_OE(uc_1_z_oe));  // open: TTYIN_CP, TTYIN_OE, uIR0, uIR1, uAddr, uPC, stage, uData
  not not_2 (not_2_out, uc_1_addr_oe);
  pc pc_1 (.PC_INC(uc_1_pc_inc), .RESET(RESET), .PC_SPE(uc_1_pc_spe), .OE(not_2_out), .PC(pc_1_pc));  // open: ADDR
  Terminal terminal_1 (.D(uc_1_data), .C(uc_1_ttyout_cp), .en(1'b1));
  Switch switch_1 (.A(uc_1_ttyout_cp), .B(switch_1_b));
  Break #(.Cycles(10000000)) BREAK_ON_TTYOUT (.brk(switch_1_b));
  memory memory_1 (
    .MEM_CP(uc_1_mem_cp), .ADDR_OE(uc_1_addr_oe), .A0_CP(uc_1_a0_cp), .A1_CP(uc_1_a1_cp), .A2_CP(uc_1_a2_cp),
    .MEM_OE(uc_1_mem_oe), .DATA(uc_1_data), .ADDR(pc_1_pc));  // open: DATA_2, ADDR_2
  \reg  W (.IO(uc_1_data), .OE(uc_1_w_oe), .CP(uc_1_w_cp));
  \reg  X (.IO(uc_1_data), .OE(uc_1_x_oe), .CP(uc_1_x_cp));
  \reg  Y (.IO(uc_1_data), .OE(uc_1_y_oe), .CP(uc_1_y_cp));
  \reg  Z (.IO(uc_1_data), .OE(uc_1_z_oe), .CP(uc_1_z_cp));
  alu alu_1 (.ALU_OP(uc_1_alu_op), .ALU_OE(uc_1_alu_oe), .ALU_CP(uc_1_alu_cp), .IN1_CP(uc_1_in1_cp), .DATA(uc_1_data));

  // Notes on the sheet:
  //   RESET: default 1
  //   clk: Hz: 10000
  //   4A
  //   4B
  //   4Y
  //   6A
  //   6Y
  //   3A
  //   3Y
endmodule
